// Digital circuit CPU.dig as structural Verilog
module CPU (
  input  [7:0] value,
  input  [1:0] dest,
  input  [1:0] src,
  input  tworeg,
  output [31:0] r0,
  output [31:0] r1,
  output [31:0] r2,
  output [31:0] r3,
  output [1:0] rd,
  output [1:0] rd_2,
  output [31:0] L,
  output [1:0] rs,
  output [31:0] target,
  output [3:0] PC,
  output [31:0] R,
  output [1:0] rd_3,
  output [1:0] rs_2,
  output [31:0] R_2
);

  wire add, add_out, Advance_out, assembler_1_p10, assembler_1_p11, decoder_1_p1, decoder_1_p2,
       decoder_1_p11, execute_1_p4, fecthc_counter_1_p7, instdisplay_1_p1, instdisplay_1_p2,
       instdisplay_1_p3, instdisplay_1_p4, instdisplay_1_p5, instdisplay_1_p6, jump, jump_out, mode_out,
       move, move_out, not_1_out, pm_1_p6, pm_1_p7, pm_1_p8, regdisplay_1_p1, regdisplay_1_p2,
       regdisplay_2_p1, regdisplay_2_p2, tworeg_t, valdisplay_1_p4, valdisplay_1_p6, valdisplay_1_p8,
       valdisplay_1_p10, valdisplay_1_p12, valdisplay_1_p14, valdisplay_1_p16, valdisplay_1_p18,
       valdisplay_2_p4, valdisplay_2_p6, valdisplay_2_p8, valdisplay_2_p10, valdisplay_2_p12,
       valdisplay_2_p14, valdisplay_2_p16, valdisplay_2_p18;
  wire [2:0] op;
  wire [3:0] pm_1_p4, valdisplay_1_p3, valdisplay_1_p5, valdisplay_1_p7, valdisplay_1_p9, valdisplay_1_p11,
       valdisplay_1_p13, valdisplay_1_p15, valdisplay_1_p17, valdisplay_2_p3, valdisplay_2_p5,
       valdisplay_2_p7, valdisplay_2_p9, valdisplay_2_p11, valdisplay_2_p13, valdisplay_2_p15,
       valdisplay_2_p17;
  wire [15:0] instdisplay_1_d1, instdisplay_1_d2, instdisplay_1_d3, instdisplay_1_d4, instdisplay_1_d5,
       instdisplay_1_d6, pm_1_p5, PROGRAM_d, regdisplay_1_d1, regdisplay_1_d2, regdisplay_2_d1,
       regdisplay_2_d2;

  SixteenSeg sixteenseg_1 (.led(regdisplay_1_d1), .dp(regdisplay_1_p1));
  REGDISPLAY regdisplay_1 (
    .D1(regdisplay_1_d1), .P1(regdisplay_1_p1), .D2(regdisplay_1_d2), .P2(regdisplay_1_p2), .E(1'b1),
    .J(jump), .R(rd));
  SixteenSeg sixteenseg_2 (.led(regdisplay_1_d2), .dp(regdisplay_1_p2));
  Seven_Seg_Hex seven_seg_hex_1 (.d(valdisplay_1_p3), .dp(valdisplay_1_p4));
  not not_1 (not_1_out, jump);
  // valdisplay valdisplay_1: pin names not known; wires that end beside it: not_1_out, L, valdisplay_1_p3, valdisplay_1_p4, valdisplay_1_p5, valdisplay_1_p6, valdisplay_1_p7, valdisplay_1_p8, valdisplay_1_p9, valdisplay_1_p10, valdisplay_1_p11, valdisplay_1_p12, valdisplay_1_p13, valdisplay_1_p14, valdisplay_1_p15, valdisplay_1_p16, valdisplay_1_p17, valdisplay_1_p18
  Seven_Seg_Hex seven_seg_hex_2 (.d(valdisplay_1_p5), .dp(valdisplay_1_p6));
  Seven_Seg_Hex seven_seg_hex_3 (.d(valdisplay_1_p7), .dp(valdisplay_1_p8));
  LED programming (.in(mode_out));
  DipSwitch mode (.out(mode_out));
  Button u_add (.out(add_out));
  Button u_move (.out(move_out));
  Button u_jump (.out(jump_out));
  Seven_Seg_Hex seven_seg_hex_4 (.d(valdisplay_1_p9), .dp(valdisplay_1_p10));
  Seven_Seg_Hex seven_seg_hex_5 (.d(valdisplay_1_p11), .dp(valdisplay_1_p12));
  // assembler assembler_1: pin names not known; wires that end beside it: jump_out, mode_out, value, dest, src, tworeg, add_out, move_out, jump_out, assembler_1_p10, assembler_1_p11
  Seven_Seg_Hex seven_seg_hex_6 (.d(valdisplay_1_p13), .dp(valdisplay_1_p14));
  Seven_Seg_Hex seven_seg_hex_7 (.d(valdisplay_1_p15), .dp(valdisplay_1_p16));
  Seven_Seg_Hex seven_seg_hex_8 (.d(valdisplay_1_p17), .dp(valdisplay_1_p18));
  // PM pm_1: pin names not known; wires that end beside it: assembler_1_p10, assembler_1_p11, PC, pm_1_p4, pm_1_p5, pm_1_p6, pm_1_p7, pm_1_p8
  EEPROMDualPort #(.AddrBits(4), .Bits(16)) PROGRAM (
    .A(pm_1_p4), .Din(pm_1_p5), .str(pm_1_p6), .C(pm_1_p7), .ld(pm_1_p8), .D(PROGRAM_d));
  SixteenSeg sixteenseg_3 (.led(instdisplay_1_d1), .dp(instdisplay_1_p1));
  SixteenSeg sixteenseg_4 (.led(instdisplay_1_d2), .dp(instdisplay_1_p2));
  instdisplay instdisplay_1 (
    .D1(instdisplay_1_d1), .P1(instdisplay_1_p1), .D2(instdisplay_1_d2), .P2(instdisplay_1_p2),
    .D3(instdisplay_1_d3), .P3(instdisplay_1_p3), .D4(instdisplay_1_d4), .P4(instdisplay_1_p4),
    .D5(instdisplay_1_d5), .P5(instdisplay_1_p5), .D6(instdisplay_1_d6), .P6(instdisplay_1_p6), .i(op));
  SixteenSeg sixteenseg_5 (.led(instdisplay_1_d3), .dp(instdisplay_1_p3));
  SixteenSeg sixteenseg_6 (.led(instdisplay_1_d4), .dp(instdisplay_1_p4));
  Button Advance (.out(Advance_out));
  SixteenSeg sixteenseg_7 (.led(instdisplay_1_d5), .dp(instdisplay_1_p5));
  SixteenSeg sixteenseg_8 (.led(instdisplay_1_d6), .dp(instdisplay_1_p6));
  // fecthc_counter fecthc_counter_1: pin names not known; wires that end beside it: mode_out, assembler_1_p10, PROGRAM_d, Advance_out, R, jump, fecthc_counter_1_p7, PC
  Seven_Seg_Hex seven_seg_hex_9 (.d(valdisplay_2_p3), .dp(valdisplay_2_p4));
  Seven_Seg_Hex seven_seg_hex_10 (.d(valdisplay_2_p5), .dp(valdisplay_2_p6));
  Seven_Seg_Hex seven_seg_hex_11 (.d(valdisplay_2_p7), .dp(valdisplay_2_p8));
  // valdisplay valdisplay_2: pin names not known; wires that end beside it: 1'b1, R, valdisplay_2_p3, valdisplay_2_p4, valdisplay_2_p5, valdisplay_2_p6, valdisplay_2_p7, valdisplay_2_p8, valdisplay_2_p9, valdisplay_2_p10, valdisplay_2_p11, valdisplay_2_p12, valdisplay_2_p13, valdisplay_2_p14, valdisplay_2_p15, valdisplay_2_p16, valdisplay_2_p17, valdisplay_2_p18
  // decoder decoder_1: pin names not known; wires that end beside it: decoder_1_p1, decoder_1_p2, fecthc_counter_1_p7, rs, rd, L, R, add, jump, move, decoder_1_p11, op, tworeg_t
  Seven_Seg_Hex seven_seg_hex_12 (.d(valdisplay_2_p9), .dp(valdisplay_2_p10));
  Seven_Seg_Hex seven_seg_hex_13 (.d(valdisplay_2_p11), .dp(valdisplay_2_p12));
  Seven_Seg_Hex seven_seg_hex_14 (.d(valdisplay_2_p13), .dp(valdisplay_2_p14));
  Seven_Seg_Hex seven_seg_hex_15 (.d(valdisplay_2_p15), .dp(valdisplay_2_p16));
  Seven_Seg_Hex seven_seg_hex_16 (.d(valdisplay_2_p17), .dp(valdisplay_2_p18));
  SixteenSeg sixteenseg_9 (.led(regdisplay_2_d1), .dp(regdisplay_2_p1));
  SixteenSeg sixteenseg_10 (.led(regdisplay_2_d2), .dp(regdisplay_2_p2));
  REGDISPLAY regdisplay_2 (
    .D1(regdisplay_2_d1), .P1(regdisplay_2_p1), .D2(regdisplay_2_d2), .P2(regdisplay_2_p2), .E(tworeg_t),
    .J(1'b0), .R(rs));
  // execute execute_1: pin names not known; wires that end beside it: L, R, decoder_1_p11, execute_1_p4
  // reg_file reg_file_1: pin names not known; wires that end beside it: rs, rd, execute_1_p4, Advance_out, decoder_1_p1, decoder_1_p2, r0, r1, r2, r3
  LED led_1 (.in(jump));
  LED led_2 (.in(add));
  LED led_3 (.in(move));

  assign R_2 = R;
  assign rd_2 = rd;
  assign rd_3 = rd;
  assign rs_2 = rs;
  assign target = R;

  // Notes on the sheet:
  //   value: default 1
  //   dest: default 1
  //   src: default 1
  //   tworeg: default 1
  //   0. R2=R2+1
  //   1. R2=R1+R2
  //   2. R3=R2
  //   3. R1=R1+R2
  //   4. R3=R1
  //   5. JUMP 1
  //   contents of PROGRAM (hex, n*v repeats v):
  //   1a0,61,bd,91,10e,10e
  //   jump
  //   add
  //   move
  //   R
  //   pc =
  //   =
  //   (R               )
  //   +
endmodule
