// Digital circuit decoder.dig as structural Verilog
module decoder (
  input  [15:0] rsval,
  input  [15:0] rdval,
  input  [31:0] inst,
  output [1:0] rs,
  output [1:0] rd,
  output [15:0] L,
  output [15:0] R,
  output add,
  output jump
);

  Multiplexer #(.Bits(16)) multiplexer_1 (.sel(inst[27]), .in_0(inst[15:0]), .in_1(rsval), .out(R));
  Multiplexer #(.Bits(16)) multiplexer_2 (.sel(inst[27]), .in_0(rsval), .in_1(rdval), .out(L));
  Decoder #(.Selector_Bits(3)) decoder_1 (
    .sel(inst[26:24]), .out_0(add), .out_7(jump));  // open: out_1, out_2, out_3, out_4, out_5, out_6

  assign rd = inst[17:16];
  assign rs = inst[21:20];
endmodule
