// Digital circuit execute.dig as structural Verilog
module execute (
  input  [31:0] L,
  input  [31:0] R,
  input  [1:0] result_mux,
  output [31:0] result
);

  wire [31:0] Add_s;

  Add #(.Bits(32)) Add (.a(L), .b(R), .c_i(1'b0), .s(Add_s));  // open: c_o
  Multiplexer #(.Selector_Bits(2), .Bits(32)) multiplexer_1 (
    .sel(result_mux), .in_0(L), .in_1(Add_s), .in_2(R), .in_3({32{1'b0}}), .out(result));

  // Notes on the sheet:
  //   L: default 1
  //   R: default 2
endmodule
