// Digital circuit multiple_adder.dig as structural Verilog
module multiple_adder (
  input  [15:0] A,
  input  [15:0] B,
  input  [15:0] C,
  input  [15:0] D,
  input  [15:0] E,
  input  [15:0] F,
  input  [15:0] G,
  input  [15:0] H,
  output [15:0] r0,
  output [15:0] r1,
  output [15:0] r2,
  output [15:0] r3,
  output [15:0] B_2
);

  wire button_1_out, decoder_1_p2, decoder_1_p3, execute_1_p3;
  wire [1:0] PC_out;
  wire [31:0] multiplexer_1_out;

  Button button_1 (.out(button_1_out));
  Multiplexer #(.Selector_Bits(2), .Bits(32)) multiplexer_1 (
    .sel(PC_out), .in_0({B, A}), .in_1({D, C}), .in_2({F, E}), .in_3({H, G}), .out(multiplexer_1_out));
  Counter #(.Bits(2)) PC (.en(1'b1), .C(button_1_out), .clr(1'b0), .out(PC_out));  // open: ovf
  // decoder decoder_1: pin names not known; wires that end beside it: multiplexer_1_out, decoder_1_p2, decoder_1_p3
  // execute execute_1: pin names not known; wires that end beside it: decoder_1_p2, decoder_1_p3, execute_1_p3, PC_out
  // reg_file reg_file_1: pin names not known; wires that end beside it: PC_out, PC_out, execute_1_p3, button_1_out, B_2, r0, r1, r2, r3

  // Notes on the sheet:
  //   A: default 1
  //   B: default 2
  //   C: default 3
  //   D: default 4
  //   E: default 5
  //   F: default 6
  //   G: default 7
  //   H: default 8
endmodule
